// Logisim project 3_bit_counter.circ as structural Verilog: 1 circuit, main circuit main
module main (
  input  M,
  input  T1,
  output msb,
  output out_4,
  output lsb
);

  wire _1_qn, _2_qn, _3_qn, and_1_out, and_2_out, and_3_out, and_4_out, clock_1_out, not_1_out, or_1_out,
       or_2_out;

  Clock clock_1 (.out(clock_1_out));
  not not_1 (not_1_out, M);
  T_Flip_Flop _1 (.clk(clock_1_out), .T(T1), .Q(lsb), .Qn(_1_qn));  // open: preset, reset, en
  and and_1 (and_1_out, not_1_out, lsb);
  and and_2 (and_2_out, M, _1_qn);
  T_Flip_Flop _2 (.clk(clock_1_out), .T(or_1_out), .Q(out_4), .Qn(_2_qn));  // open: preset, reset, en
  or or_1 (or_1_out, and_1_out, and_2_out);
  and and_3 (and_3_out, and_1_out, out_4);
  and and_4 (and_4_out, _2_qn, and_2_out);
  T_Flip_Flop _3 (.clk(clock_1_out), .T(or_2_out), .Q(msb), .Qn(_3_qn));  // open: preset, reset, en
  or or_2 (or_2_out, and_3_out, and_4_out);

  // Notes on the sheet:
  //   3 BIT UP/DOWN COUNTER USING 3 T FLIP-FLOPS
endmodule
