// Logisim project 3_bit_magnitude_comparator.circ as structural Verilog: 1 circuit, main circuit main
module main (
  input  A2,
  input  B2,
  input  A1,
  input  B1,
  input  A0,
  input  B0,
  output A_B,
  output A_B_2,
  output A_B_3
);

  wire and_1_out, and_2_out, and_3_out, and_4_out, and_5_out, and_6_out, not_1_out, not_2_out, not_3_out,
       not_4_out, not_5_out, not_6_out, xnor_1_out, xnor_2_out, xnor_3_out;

  not not_1 (not_1_out, B2);
  not not_2 (not_2_out, B1);
  not not_3 (not_3_out, B0);
  xnor xnor_1 (xnor_1_out, A2, B2);
  xnor xnor_2 (xnor_2_out, A1, B1);
  xnor xnor_3 (xnor_3_out, A0, B0);
  not not_4 (not_4_out, A0);
  not not_5 (not_5_out, A1);
  not not_6 (not_6_out, A2);
  and and_1 (and_1_out, A2, not_1_out);
  and and_2 (and_2_out, xnor_1_out, A1, not_2_out);
  and and_3 (and_3_out, xnor_1_out, A0, xnor_2_out, not_3_out);
  and and_4 (and_4_out, xnor_2_out, B0, not_4_out, xnor_1_out);
  and and_5 (and_5_out, xnor_1_out, B1, not_5_out);
  and and_6 (and_6_out, B2, not_6_out);
  or or_1 (A_B, and_1_out, and_2_out, and_3_out);
  and and_7 (A_B_2, xnor_1_out, xnor_2_out, xnor_3_out);
  or or_2 (A_B_3, and_4_out, and_5_out, and_6_out);

  // Notes on the sheet:
  //   3 BIT MAGNITUDE COMPARATOR
endmodule
