// Logisim project 4-bit-jk-flipflop-counter (3).circ as structural Verilog: 1 circuit, main circuit main
module main (
);

  wire button_1_out, clock_1_out, j_k_ff_1_q, j_k_ff_2_q, j_k_ff_3_q, j_k_ff_4_q;

  Clock clock_1 (.out(clock_1_out));
  Button button_1 (.out(button_1_out));
  J_K_Flip_Flop j_k_ff_1 (
    .J(1'b1), .clk(clock_1_out), .K(1'b1), .Q(j_k_ff_1_q), .reset(button_1_out));  // open: Qn, preset, en
  LED led_1 (.in(j_k_ff_3_q));
  LED led_2 (.in(j_k_ff_4_q));
  J_K_Flip_Flop j_k_ff_2 (
    .J(1'b1), .clk(j_k_ff_1_q), .K(1'b1), .Q(j_k_ff_2_q), .reset(button_1_out));  // open: Qn, preset, en
  LED led_3 (.in(j_k_ff_1_q));
  LED led_4 (.in(j_k_ff_2_q));
  J_K_Flip_Flop j_k_ff_3 (
    .J(1'b1), .clk(j_k_ff_2_q), .K(1'b1), .Q(j_k_ff_3_q), .reset(button_1_out));  // open: Qn, preset, en
  J_K_Flip_Flop j_k_ff_4 (
    .J(1'b1), .clk(j_k_ff_3_q), .K(1'b1), .Q(j_k_ff_4_q), .reset(button_1_out));  // open: Qn, preset, en

  // Notes on the sheet:
  //   4 bit JK flip flop counter
endmodule
