// Logisim project DDS_MAIN_PROJECT.circ as structural Verilog: 11 circuits, main circuit main
module main (
  input  in_1,
  input  in_2,
  input  in_3,
  input  in_4,
  input  [3:0] B_Present_output_from_ADC,
  output out_6,
  output out_7,
  output out_8,
  output out_9
);

  wire clock_1_out, n4bit_comparator_1_a_b;
  wire [3:0] n4bit_register_1__4_bit_output;

  _4bit_register u_4bit_register_1 (
    .A3(in_1), .A2(in_2), .A1(in_3), .A0(in_4), ._4_bit_output(n4bit_register_1__4_bit_output));  // open: Q3_prime, Q2_prime, Q1_prime, Q0_prime
  _4bit_Comparator u_4bit_comparator_1 (
    .A(n4bit_register_1__4_bit_output), .B(B_Present_output_from_ADC), .A_B(n4bit_comparator_1_a_b));  // open: A_B_2, A_B_3
  Clock clock_1 (.out(clock_1_out));
  _4bit_counter u_4bit_counter_1 (
    .M(n4bit_comparator_1_a_b), .Clk(clock_1_out), .A0(out_9), .A1(out_8), .A2(out_7), .A3(out_6));
endmodule

module _4bit_counter (
  input  M,
  input  Clk,
  output A0,
  output A1,
  output A3,
  output A2
);

  wire and_1_out, and_2_out, and_3_out, and_4_out, and_5_out, and_6_out, j_k_ff_1_qn, j_k_ff_2_qn,
       j_k_ff_3_qn, not_1_out, or_1_out, or_2_out, or_3_out;

  not not_1 (not_1_out, M);
  J_K_Flip_Flop #(.trigger("falling")) j_k_ff_1 (
    .J(1'b1), .clk(Clk), .K(1'b1), .Q(A0), .Qn(j_k_ff_1_qn));  // open: preset, en, reset
  and and_1 (and_1_out, not_1_out, A0);
  and and_2 (and_2_out, M, j_k_ff_1_qn);
  or or_1 (or_1_out, and_1_out, and_2_out);
  J_K_Flip_Flop #(.trigger("falling")) j_k_ff_2 (
    .J(1'b1), .clk(or_1_out), .K(1'b1), .Q(A1), .Qn(j_k_ff_2_qn));  // open: preset, en, reset
  and and_3 (and_3_out, not_1_out, A1);
  and and_4 (and_4_out, M, j_k_ff_2_qn);
  or or_2 (or_2_out, and_3_out, and_4_out);
  J_K_Flip_Flop #(.trigger("falling")) j_k_ff_3 (
    .J(1'b1), .clk(or_2_out), .K(1'b1), .Q(A2), .Qn(j_k_ff_3_qn));  // open: preset, en, reset
  and and_5 (and_5_out, not_1_out, A2);
  or or_3 (or_3_out, and_5_out, and_6_out);
  and and_6 (and_6_out, M, j_k_ff_3_qn);
  J_K_Flip_Flop #(.trigger("falling")) j_k_ff_4 (
    .J(1'b1), .clk(or_3_out), .K(1'b1), .Q(A3));  // open: Qn, preset, en, reset

  // Notes on the sheet:
  //   M'
  //   4 bit J-K Flip Flop Asynchronous Up/Down Counter
endmodule

module _4bit_register (
  input  A3,
  input  A2,
  input  A1,
  input  A0,
  output Q3_prime,
  output Q2_prime,
  output [3:0] _4_bit_output,
  output Q1_prime,
  output Q0_prime
);

  wire Clk_out;

  Clock Clk (.out(Clk_out));
  D_Flip_Flop d_ff_1 (.clk(Clk_out), .D(A3), .Q(_4_bit_output[3]), .Qn(Q3_prime));  // open: preset, en, reset
  D_Flip_Flop d_ff_2 (.clk(Clk_out), .D(A2), .Q(_4_bit_output[2]), .Qn(Q2_prime));  // open: preset, en, reset
  D_Flip_Flop d_ff_3 (.clk(Clk_out), .D(A1), .Q(_4_bit_output[1]), .Qn(Q1_prime));  // open: preset, en, reset
  D_Flip_Flop d_ff_4 (.clk(Clk_out), .D(A0), .Q(_4_bit_output[0]), .Qn(Q0_prime));  // open: preset, en, reset

  // Notes on the sheet:
  //   4 bit Register using D Flip Flops
endmodule

module _4bit_Comparator (
  input  [3:0] A,
  input  [3:0] B,
  output A_B,
  output A_B_2,
  output A_B_3
);

  Comparator #(.width(4)) comparator_1 (.a(A), .b(B), .gt(A_B), .eq(A_B_2), .lt(A_B_3));

  // Notes on the sheet:
  //   4-bit comparator
endmodule

module _4digit_LED_A (
  input  I4,
  input  I3,
  input  I2,
  input  I1,
  output out_5
);

  wire and_1_out, and_2_out, and_3_out, not_1_out, not_2_out, not_3_out, not_4_out, xor_1_out;

  not not_1 (not_1_out, I4);
  not not_2 (not_2_out, I3);
  not not_3 (not_3_out, I2);
  not not_4 (not_4_out, I1);
  xor xor_1 (xor_1_out, I4, I2);
  and and_1 (and_1_out, I4, not_2_out, I2, not_4_out);
  and and_2 (and_2_out, I3, I1);
  and and_3 (and_3_out, not_1_out, not_2_out, not_3_out, not_4_out);
  or or_1 (out_5, xor_1_out, and_1_out, and_2_out, and_3_out);

  // Notes on the sheet:
  //   I3
  //   I4
  //   I2
  //   I4'
  //   I1
  //   I3'
  //   I2'
  //   I1'
endmodule

module _4digit_LED_B (
  input  I4,
  input  I3,
  input  I2,
  input  I1,
  output out_5
);

  wire and_1_out, and_2_out, and_3_out, and_4_out, not_1_out, not_2_out, not_3_out, not_4_out;

  not not_1 (not_1_out, I4);
  not not_2 (not_2_out, I3);
  not not_3 (not_3_out, I2);
  not not_4 (not_4_out, I1);
  and and_1 (and_1_out, I4, not_3_out);
  and and_2 (and_2_out, not_3_out, not_4_out);
  and and_3 (and_3_out, I4, not_4_out);
  and and_4 (and_4_out, not_1_out, I2, I1);
  or or_1 (out_5, not_2_out, and_1_out, and_2_out, and_3_out, and_4_out);

  // Notes on the sheet:
  //   I3
  //   I4
  //   I2
  //   I4'
  //   I1
  //   I2'
  //   I3'
  //   I1'
endmodule

module _4digit_LED_C (
  input  I4,
  input  I3,
  input  I2,
  input  I1,
  output out_5
);

  wire and_1_out, and_2_out, not_1_out, not_2_out, not_3_out, not_4_out, xor_1_out;

  not not_1 (not_1_out, I4);
  not not_2 (not_2_out, I3);
  not not_3 (not_3_out, I2);
  not not_4 (not_4_out, I1);
  xor xor_1 (xor_1_out, I4, I3);
  and and_1 (and_1_out, I4, I3, I2);
  and and_2 (and_2_out, not_1_out, not_2_out, not_3_out);
  or or_1 (out_5, xor_1_out, and_1_out, and_2_out, I1);

  // Notes on the sheet:
  //   I3
  //   I4
  //   I2
  //   I4'
  //   I1
  //   I3'
  //   I2'
  //   I1'
endmodule

module _4digit_LED_D (
  input  I4,
  input  I3,
  input  I2,
  input  I1,
  output out_5
);

  wire and_1_out, and_2_out, and_3_out, and_4_out, and_5_out, not_1_out, not_2_out, not_3_out, not_4_out;

  not not_1 (not_1_out, I4);
  not not_2 (not_2_out, I3);
  not not_3 (not_3_out, I2);
  not not_4 (not_4_out, I1);
  and and_1 (and_1_out, I4, I3, not_3_out);
  and and_2 (and_2_out, not_1_out, not_2_out, I2);
  and and_3 (and_3_out, I3, not_3_out, I1);
  and and_4 (and_4_out, I4, I3, I1);
  and and_5 (and_5_out, not_2_out, not_4_out);
  or or_1 (out_5, and_1_out, and_2_out, and_3_out, and_4_out, and_5_out);

  // Notes on the sheet:
  //   I3
  //   I2
  //   I4
  //   I4'
  //   I1
  //   I3'
  //   I2'
  //   I1'
  //   T O BE CORRECTED
  //   W
  //   W
  //   W
  //   W
  //   W
endmodule

module _4digit_LED_E (
  input  i4,
  input  I3,
  input  I2,
  input  I1,
  output out_5
);

  wire and_1_out, and_2_out, and_3_out, not_1_out, not_2_out, not_3_out, not_4_out;

  not not_1 (not_1_out, i4);
  not not_2 (not_2_out, I3);
  not not_3 (not_3_out, I2);
  not not_4 (not_4_out, I1);
  and and_1 (and_1_out, I2, not_4_out, not_1_out);
  and and_2 (and_2_out, not_3_out, not_4_out, i4);
  and and_3 (and_3_out, not_2_out, not_4_out);
  or or_1 (out_5, and_1_out, and_2_out, and_3_out);

  // Notes on the sheet:
  //   I1
  //   I2
  //   I3
  //   I4
  //   I2'
  //   I3'
  //   I1'
  //   I4'
endmodule

module _4_digit_LED_F (
  input  i4,
  input  I3,
  input  I2,
  input  I1,
  output out_5
);

  wire and_1_out, and_2_out, and_3_out, and_4_out, and_5_out, and_6_out, not_1_out, not_2_out, not_3_out,
       not_4_out;

  not not_1 (not_1_out, i4);
  not not_2 (not_2_out, I3);
  not not_3 (not_3_out, I2);
  not not_4 (not_4_out, I1);
  and and_1 (and_1_out, not_4_out, not_3_out, not_1_out);
  and and_2 (and_2_out, not_1_out, I3, not_3_out);
  and and_3 (and_3_out, I2, not_4_out, I3);
  and and_4 (and_4_out, i4, I3, I2);
  and and_5 (and_5_out, i4, not_2_out, not_3_out);
  and and_6 (and_6_out, not_4_out, I2, i4);
  or or_1 (out_5, and_1_out, and_2_out, and_3_out, and_4_out, and_5_out, and_6_out);

  // Notes on the sheet:
  //   I2
  //   I1
  //   I4
  //   I3
  //   I2'
  //   I3'
  //   I1'
  //   I4'
endmodule

module _4_digit_LED_G (
  input  i4,
  input  I3,
  input  I2,
  input  I1,
  output out_5
);

  wire and_1_out, and_2_out, and_3_out, and_4_out, and_5_out, not_1_out, not_2_out, not_3_out, not_4_out;

  not not_1 (not_1_out, i4);
  not not_2 (not_2_out, I3);
  not not_3 (not_3_out, I2);
  not not_4 (not_4_out, I1);
  and and_1 (and_1_out, not_1_out, not_4_out, I2);
  and and_2 (and_2_out, not_1_out, not_2_out, I2);
  and and_3 (and_3_out, i4, I3, I2);
  and and_4 (and_4_out, I3, not_3_out);
  and and_5 (and_5_out, i4, not_3_out);
  or or_1 (out_5, and_1_out, and_2_out, and_3_out, and_4_out, and_5_out);

  // Notes on the sheet:
  //   I1
  //   I2
  //   I3
  //   I4
  //   I2'
  //   I3'
  //   I1'
  //   I4'
endmodule
