// Logisim project DDS_PROJECT.circ as structural Verilog: 11 circuits, main circuit main
module main (
  input  in_1,
  input  in_2,
  input  in_3,
  input  in_4,
  input  [3:0] B_Present_output_from_ADC
);

  wire CLK_out, clock_1_out, n4_digit_led_f_1_out_5, n4_digit_led_g_1_out_5, n4bit_comparator_1_a_b,
       n4bit_counter_1_a0, n4bit_counter_1_a1, n4bit_counter_1_a2, n4bit_counter_1_a3, n4digit_led_a_1_out_5,
       n4digit_led_b_1_out_5, n4digit_led_c_1_out_5, n4digit_led_d_1_out_5, n4digit_led_e_1_out_5, not_1_out;
  wire [3:0] n4bit_register_1__4_bit_output;

  Clock CLK (.out(CLK_out));
  _4bit_register u_4bit_register_1 (
    .A3(in_1), .A2(in_2), .A1(in_3), .A0(in_4), .ClK_INPUT(CLK_out),
    ._4_bit_output(n4bit_register_1__4_bit_output));  // open: Q3_prime, Q2_prime, Q1_prime, Q0_prime
  _4bit_Comparator u_4bit_comparator_1 (
    .A(n4bit_register_1__4_bit_output), .B(B_Present_output_from_ADC), .A_B(n4bit_comparator_1_a_b));  // open: A_B_2, A_B_3
  not not_1 (not_1_out, n4bit_comparator_1_a_b);
  Clock clock_1 (.out(clock_1_out));
  _4bit_counter u_4bit_counter_1 (
    .M(not_1_out), .Clk(clock_1_out), .A0(n4bit_counter_1_a0), .A1(n4bit_counter_1_a1),
    .A2(n4bit_counter_1_a2), .A3(n4bit_counter_1_a3));
  _4digit_LED_A u_4digit_led_a_1 (
    .I4(n4bit_counter_1_a3), .I3(n4bit_counter_1_a2), .I2(n4bit_counter_1_a1), .I1(n4bit_counter_1_a0),
    .out_5(n4digit_led_a_1_out_5));
  _4digit_LED_B u_4digit_led_b_1 (
    .I4(n4bit_counter_1_a3), .I3(n4bit_counter_1_a2), .I2(n4bit_counter_1_a1), .I1(n4bit_counter_1_a0),
    .out_5(n4digit_led_b_1_out_5));
  _4digit_LED_C u_4digit_led_c_1 (
    .I4(n4bit_counter_1_a3), .I3(n4bit_counter_1_a2), .I2(n4bit_counter_1_a1), .I1(n4bit_counter_1_a0),
    .out_5(n4digit_led_c_1_out_5));
  _4digit_LED_D u_4digit_led_d_1 (
    .I4(n4bit_counter_1_a3), .I3(n4bit_counter_1_a2), .I2(n4bit_counter_1_a1), .I1(n4bit_counter_1_a0),
    .out_5(n4digit_led_d_1_out_5));
  _4digit_LED_E u_4digit_led_e_1 (
    .i4(n4bit_counter_1_a3), .I3(n4bit_counter_1_a2), .I2(n4bit_counter_1_a1), .I1(n4bit_counter_1_a0),
    .out_5(n4digit_led_e_1_out_5));
  _4_digit_LED_F u_4_digit_led_f_1 (
    .i4(n4bit_counter_1_a3), .I3(n4bit_counter_1_a2), .I2(n4bit_counter_1_a1), .I1(n4bit_counter_1_a0),
    .out_5(n4_digit_led_f_1_out_5));
  _4_digit_LED_G u_4_digit_led_g_1 (
    .i4(n4bit_counter_1_a3), .I3(n4bit_counter_1_a2), .I2(n4bit_counter_1_a1), .I1(n4bit_counter_1_a0),
    .out_5(n4_digit_led_g_1_out_5));
  _7_Segment_Display u_7_segment_display_1 (
    .g(n4_digit_led_g_1_out_5), .f(n4_digit_led_f_1_out_5), .a(n4digit_led_a_1_out_5),
    .b(n4digit_led_b_1_out_5), .e(n4digit_led_e_1_out_5), .d(n4digit_led_d_1_out_5), .c(n4digit_led_c_1_out_5));  // open: dp

  // Notes on the sheet:
  //   UP COUNTING if A>B
  //   DOWN COUNTING IF B>A
  //   A-Previous output from ADC
  //   I1
  //   I4
  //   I3
  //   I2
endmodule

// COUNT
module _4bit_counter (
  input  M,
  input  Clk,
  output A0,
  output A1,
  output A3,
  output A2
);

  wire and_1_out, and_2_out, and_3_out, and_4_out, and_5_out, and_6_out, j_k_ff_1_qn, j_k_ff_2_qn,
       j_k_ff_3_qn, not_1_out, or_1_out, or_2_out, or_3_out;

  not not_1 (not_1_out, M);
  J_K_Flip_Flop #(.trigger("falling")) j_k_ff_1 (
    .J(1'b1), .clk(Clk), .K(1'b1), .Q(A0), .Qn(j_k_ff_1_qn));  // open: preset, en, reset
  and and_1 (and_1_out, not_1_out, A0);
  and and_2 (and_2_out, M, j_k_ff_1_qn);
  or or_1 (or_1_out, and_1_out, and_2_out);
  J_K_Flip_Flop #(.trigger("falling")) j_k_ff_2 (
    .J(1'b1), .clk(or_1_out), .K(1'b1), .Q(A1), .Qn(j_k_ff_2_qn));  // open: preset, en, reset
  and and_3 (and_3_out, not_1_out, A1);
  and and_4 (and_4_out, M, j_k_ff_2_qn);
  or or_2 (or_2_out, and_3_out, and_4_out);
  J_K_Flip_Flop #(.trigger("falling")) j_k_ff_3 (
    .J(1'b1), .clk(or_2_out), .K(1'b1), .Q(A2), .Qn(j_k_ff_3_qn));  // open: preset, en, reset
  and and_5 (and_5_out, not_1_out, A2);
  or or_3 (or_3_out, and_5_out, and_6_out);
  and and_6 (and_6_out, M, j_k_ff_3_qn);
  J_K_Flip_Flop #(.trigger("falling")) j_k_ff_4 (
    .J(1'b1), .clk(or_3_out), .K(1'b1), .Q(A3));  // open: Qn, preset, en, reset

  // Notes on the sheet:
  //   M'
  //   4 bit J-K Flip Flop Asynchronous Up/Down Counter
endmodule

// REG
module _4bit_register (
  input  A3,
  input  A2,
  input  A1,
  input  A0,
  input  ClK_INPUT,
  output Q3_prime,
  output Q2_prime,
  output [3:0] _4_bit_output,
  output Q1_prime,
  output Q0_prime
);

  D_Flip_Flop d_ff_1 (.clk(ClK_INPUT), .D(A3), .Q(_4_bit_output[3]), .Qn(Q3_prime));  // open: preset, en, reset
  D_Flip_Flop d_ff_2 (.clk(ClK_INPUT), .D(A2), .Q(_4_bit_output[2]), .Qn(Q2_prime));  // open: preset, en, reset
  D_Flip_Flop d_ff_3 (.clk(ClK_INPUT), .D(A1), .Q(_4_bit_output[1]), .Qn(Q1_prime));  // open: preset, en, reset
  D_Flip_Flop d_ff_4 (.clk(ClK_INPUT), .D(A0), .Q(_4_bit_output[0]), .Qn(Q0_prime));  // open: preset, en, reset

  // Notes on the sheet:
  //   4 bit Register using D Flip Flops
endmodule

// COM
module _4bit_Comparator (
  input  [3:0] A,
  input  [3:0] B,
  output A_B,
  output A_B_2,
  output A_B_3
);

  Comparator #(.width(4)) comparator_1 (.a(A), .b(B), .gt(A_B), .eq(A_B_2), .lt(A_B_3));

  // Notes on the sheet:
  //   4-bit comparator
endmodule

// A
module _4digit_LED_A (
  input  I4,
  input  I3,
  input  I2,
  input  I1,
  output out_5
);

  wire and_1_out, and_2_out, and_3_out, not_1_out, not_2_out, not_3_out, not_4_out, xor_1_out;

  not not_1 (not_1_out, I4);
  not not_2 (not_2_out, I3);
  not not_3 (not_3_out, I2);
  not not_4 (not_4_out, I1);
  xor xor_1 (xor_1_out, I4, I2);
  and and_1 (and_1_out, I4, not_2_out, I2, not_4_out);
  and and_2 (and_2_out, I3, I1);
  and and_3 (and_3_out, not_1_out, not_2_out, not_3_out, not_4_out);
  or or_1 (out_5, xor_1_out, and_1_out, and_2_out, and_3_out);

  // Notes on the sheet:
  //   I3
  //   I2
  //   I4
  //   I4'
  //   I1
  //   I3'
  //   I2'
  //   I1'
endmodule

// B
module _4digit_LED_B (
  input  I4,
  input  I3,
  input  I2,
  input  I1,
  output out_5
);

  wire and_1_out, and_2_out, and_3_out, and_4_out, not_1_out, not_2_out, not_3_out, not_4_out;

  not not_1 (not_1_out, I4);
  not not_2 (not_2_out, I3);
  not not_3 (not_3_out, I2);
  not not_4 (not_4_out, I1);
  and and_1 (and_1_out, I4, not_3_out);
  and and_2 (and_2_out, not_3_out, not_4_out);
  and and_3 (and_3_out, I4, not_4_out);
  and and_4 (and_4_out, not_1_out, I2, I1);
  or or_1 (out_5, not_2_out, and_1_out, and_2_out, and_3_out, and_4_out);

  // Notes on the sheet:
  //   I3
  //   I2
  //   I4
  //   I4'
  //   I1
  //   I3'
  //   I2'
  //   I1'
endmodule

// C
module _4digit_LED_C (
  input  I4,
  input  I3,
  input  I2,
  input  I1,
  output out_5
);

  wire and_1_out, and_2_out, not_1_out, not_2_out, not_3_out, not_4_out, xor_1_out;

  not not_1 (not_1_out, I4);
  not not_2 (not_2_out, I3);
  not not_3 (not_3_out, I2);
  not not_4 (not_4_out, I1);
  xor xor_1 (xor_1_out, I4, I3);
  and and_1 (and_1_out, I4, I3, I2);
  and and_2 (and_2_out, not_1_out, not_2_out, not_3_out);
  or or_1 (out_5, xor_1_out, and_1_out, and_2_out, I1);

  // Notes on the sheet:
  //   I3
  //   I4
  //   I2
  //   I4'
  //   I1
  //   I2'
  //   I3'
  //   I1'
endmodule

// D
module _4digit_LED_D (
  input  I4,
  input  I3,
  input  I2,
  input  I1,
  output out_5
);

  wire and_1_out, and_2_out, and_3_out, and_4_out, and_5_out, and_6_out, and_7_out, not_1_out, not_2_out,
       not_3_out, not_4_out;

  not not_1 (not_1_out, I4);
  not not_2 (not_2_out, I3);
  not not_3 (not_3_out, I2);
  not not_4 (not_4_out, I1);
  and and_1 (and_1_out, not_1_out, not_2_out, I2);
  and and_2 (and_2_out, not_1_out, I2, not_4_out);
  and and_3 (and_3_out, I4, I3, not_3_out);
  and and_4 (and_4_out, I3, not_3_out, I1);
  and and_5 (and_5_out, not_2_out, not_3_out, not_4_out);
  and and_6 (and_6_out, I4, I3, I1);
  and and_7 (and_7_out, not_2_out, I2, not_4_out);
  or or_1 (out_5, and_1_out, and_2_out, and_3_out, and_4_out, and_5_out, and_6_out, and_7_out);

  // Notes on the sheet:
  //   I3
  //   I2
  //   I4
  //   I4'
  //   I1
  //   I2'
  //   I3'
  //   I1'
endmodule

// E
module _4digit_LED_E (
  input  i4,
  input  I3,
  input  I2,
  input  I1,
  output out_5
);

  wire and_1_out, and_2_out, and_3_out, not_1_out, not_2_out, not_3_out, not_4_out;

  not not_1 (not_1_out, i4);
  not not_2 (not_2_out, I3);
  not not_3 (not_3_out, I2);
  not not_4 (not_4_out, I1);
  and and_1 (and_1_out, I2, not_4_out, not_1_out);
  and and_2 (and_2_out, not_3_out, not_4_out, i4);
  and and_3 (and_3_out, not_2_out, not_4_out);
  or or_1 (out_5, and_1_out, and_2_out, and_3_out);

  // Notes on the sheet:
  //   I2
  //   I1
  //   I3
  //   I4
  //   I2'
  //   I3'
  //   I1'
  //   I4'
endmodule

// F
module _4_digit_LED_F (
  input  i4,
  input  I3,
  input  I2,
  input  I1,
  output out_5
);

  wire and_1_out, and_2_out, and_3_out, and_4_out, and_5_out, and_6_out, not_1_out, not_2_out, not_3_out,
       not_4_out;

  not not_1 (not_1_out, i4);
  not not_2 (not_2_out, I3);
  not not_3 (not_3_out, I2);
  not not_4 (not_4_out, I1);
  and and_1 (and_1_out, not_4_out, not_3_out, not_1_out);
  and and_2 (and_2_out, not_1_out, I3, not_3_out);
  and and_3 (and_3_out, I2, not_4_out, I3);
  and and_4 (and_4_out, i4, I3, I2);
  and and_5 (and_5_out, i4, not_2_out, not_3_out);
  and and_6 (and_6_out, not_4_out, I2, i4);
  or or_1 (out_5, and_1_out, and_2_out, and_3_out, and_4_out, and_5_out, and_6_out);

  // Notes on the sheet:
  //   I1
  //   I2
  //   I4
  //   I3
  //   I2'
  //   I3'
  //   I1'
  //   I4'
endmodule

// G
module _4_digit_LED_G (
  input  i4,
  input  I3,
  input  I2,
  input  I1,
  output out_5
);

  wire and_1_out, and_2_out, and_3_out, and_4_out, and_5_out, not_1_out, not_2_out, not_3_out, not_4_out;

  not not_1 (not_1_out, i4);
  not not_2 (not_2_out, I3);
  not not_3 (not_3_out, I2);
  not not_4 (not_4_out, I1);
  and and_1 (and_1_out, not_1_out, not_4_out, I2);
  and and_2 (and_2_out, not_1_out, not_2_out, I2);
  and and_3 (and_3_out, i4, I3, I2);
  and and_4 (and_4_out, I3, not_3_out);
  and and_5 (and_5_out, i4, not_3_out);
  or or_1 (out_5, and_1_out, and_2_out, and_3_out, and_4_out, and_5_out);

  // Notes on the sheet:
  //   I1
  //   I2
  //   I4
  //   I3
  //   I2'
  //   I3'
  //   I1'
  //   I4'
endmodule
