// Logisim project SRLatch.circ as structural Verilog: 2 circuits, main circuit main
module main (
  input  R,
  input  S,
  input  R_2,
  input  S_2,
  input  R_3,
  input  S_3,
  output Q,
  output Q_prime,
  output Q_2,
  output Q_prime_2,
  output Q_3,
  output Q_prime_3
);

  nor nor_1 (Q, R, Q_prime);
  nor nor_2 (Q_prime, Q, S);
  nor nor_3 (Q_2, R_2, Q_prime_2);
  nor nor_4 (Q_prime_2, Q_2, S_2);
  nor nor_5 (Q_3, R_3, Q_prime_3);
  nor nor_6 (Q_prime_3, Q_3, S_3);

  // Notes on the sheet:
  //   3 S-R Latches to be used in an ADC for each bit
endmodule

module SRLatch_outside_adc (
  input  R,
  input  S,
  input  R_2,
  input  S_2,
  input  R_3,
  input  S_3,
  output Q,
  output Q_prime,
  output Q_2,
  output Q_prime_2,
  output Q_3,
  output Q_prime_3
);

  nor nor_1 (Q, R, Q_prime);
  nor nor_2 (Q_prime, Q, S);
  nor nor_3 (Q_2, R_2, Q_prime_2);
  nor nor_4 (Q_prime_2, Q_2, S_2);
  nor nor_5 (Q_3, R_3, Q_prime_3);
  nor nor_6 (Q_prime_3, Q_3, S_3);
endmodule
